# Fritzing sketch diy_relay_modul_schema (saved by Fritzing 0.8.7b)
breadboards: 1

parts:
  Part1 = songle relay
  Q1 = TRANSISTOR_NPN [package=to-92-ammo]
  R1 = Resistor [tolerance=±5% resistance=220 package=THT]
  U1 = TLP621 [package=THT]
  D1 = Diode [package=diode-1n4001]
  Part2 = Arduino Uno (Rev3)
  LED1 = LED - 5mm [color="Red (633nm)" package="5 mm [THT]"]
  R2 = Resistor [tolerance=±5% resistance=220 package=THT]
  LED2 = smd LED [color="Green (560nm)" package="0603 [SMD]"]
  R3 = Resistor [tolerance=±5% resistance=220 package=THT]

nets:
  VCC: Part1.VCC, U1.Pin_4, D1.A, Part2.5V, R2.Pin_1, R3.Pin_1
  N1: Part1.GND, Q1.C, LED2.cathode
  N2: Q1.E, U1.Pin_2, Part2.GND, LED1.cathode
  N3: Q1.B, R1.Pin_1
  N4: R1.Pin_0, U1.Pin_3
  N5: U1.Pin_1, Part2.D2
  N6: LED1.anode, R3.Pin_0
  N7: R2.Pin_0, LED2.anode
