# Fritzing sketch ldr_trimpot (saved by Fritzing 0.8.7b)
breadboards: 1

parts:
  R1 = Photocell (LDR) [package=THT]
  Q1 = PNP-Transistor [package="SOT-23 [SMD]"]
  R4 = Resistor [tolerance=±5% resistance=1k package=THT]
  LED1 = LED - 5mm [color="Red (633nm)" package="5 mm [THT]"]
  R5 = Resistor [tolerance=±5% resistance=1k package=THT]
  VCC1 = Battery
  R2 = TRIMPOT [package=trim_pot_pth]

nets:
  N1: R1.pin_0, R4.Pin_0, VCC1.+
  N2: R1.pin_1, R2.CCW
  N3: Q1.2, LED1.cathode
  N4: Q1.0, R5.Pin_0, R5.Pin_1, R2.WIPER
  N5: Q1.1, VCC1.-, R2.CW
  N6: R4.Pin_1, LED1.anode
