# Fritzing sketch relay_ldr (saved by Fritzing 0.8.7b)
breadboards: 2

parts:
  Part2 = songle relay
  Q1 = NPN-Transistor [package="TO92 [THT]"]
  D2 = Diode [package=diode-1n4001]
  Q2 = NPN-Transistor [package="TO92 [THT]"]
  R1 = Resistor [tolerance=±5% resistance=220 package=THT]
  R2 = Resistor [tolerance=±5% resistance=220 package=THT]
  R3 = Photocell (LDR) [package=THT]
  R7 = Rotary Potentiometer (Small)

nets:
  N1: Part2.VCC, D2.A
  N2: Part2.GND, Q1.C
  N3: Q1.B, R1.Pin_0
  N4: Q2.E, R1.Pin_1
  N5: Q2.B, R2.Pin_0, R2.Pin_1, R3.pin_1, R7.leg1
