# Fritzing sketch schematic (saved by Fritzing 0.8.7b)
breadboards: 1

parts:
  U1 = ESP8266 NodeMCU LoLin base
  LED1 = LED - 5mm [color="Red (633nm)" package="5 mm [THT]"]

nets:
  N1: U1.D1-0, U1.D1-2, LED1.anode
  N2: U1.GND3-0, LED1.cathode

custom parts:
  ESP8266 NodeMCU LoLin base: ESP8266 based NodeMCU Base
