# Fritzing sketch simple_delay_time_led (saved by Fritzing 0.8.7b)
breadboards: 1

parts:
  C1 = Electrolytic Capacitor [capacitance=1µF package="100 mil [THT, electrolytic]"]
  S1 = Pushbutton [package="[THT]"]
  R1 = Resistor [tolerance=±5% resistance=220 package=THT]  # not connected
  Q1 = PNP-Transistor [package="SOT-23 [SMD]"]
  LED3 = LED - 5mm [color="Red (633nm)" package="5 mm [THT]"]
  R2 = Resistor [tolerance=±5% resistance=220 package=THT]

nets:
  N1: C1.-, Q1.1
  N2: C1.+, S1.Pin_1, S1.Pin_2
  N3: S1.Pin_3, S1.Pin_4
  N4: Q1.2, LED3.cathode
  N5: Q1.0, R2.Pin_1
