# Fritzing sketch timer_relay_diy (saved by Fritzing 0.8.7b)
breadboards: 1

parts:
  C1 = Electrolytic Capacitor [capacitance=100µF package="200 mil [THT, electrolytic]"]
  Part1 = songle relay
  Q1 = PNP-Transistor [package="SOT-23 [SMD]"]
  D1 = Diode [package=diode-1n4148]
  R1 = Resistor [package="2010 [SMD]"]
  LED1 = smd LED [color="Red (633nm)" package="0603 [SMD]"]
  R2 = Resistor [package="2010 [SMD]"]
  S1 = Pushbutton [package="[THT]"]

nets:
  N1: C1.-, Q1.2
  N2: C1.+, R1.Pin_0, S1.Pin_3, S1.Pin_4
  N3: Part1.VCC, D1.A, R2.Pin_1, S1.Pin_1, S1.Pin_2
  N4: Part1.GND, Q1.1, D1.C, LED1.cathode
  N5: Q1.0, R1.Pin_1
  N6: LED1.anode, R2.Pin_0
