# Fritzing sketch 001. Relay RTC Modul Schema (saved by Fritzing 0.8.7b)
breadboards: 1

parts:
  PCB2 = RTC_DS1302_module
  KY-1 = Keyes Relay [package=THT]
  Part1 = Arduino Uno (Rev3)

nets:
  VCC: PCB2.VCC, KY-1.power, Part1.5V
  GND: PCB2.GND, KY-1.ground, Part1.GND
  N1: PCB2.RST, Part1.D8
  N2: PCB2.DAT, Part1.D7
  N3: PCB2.CLK, Part1.D6_PWM
  N4: KY-1.signal, Part1.D12/MISO

custom parts:
  RTC_DS1302_module: Arduino module DS1302 SPI Real Time Clock
  Keyes Relay: The Keyes 5V relay module is suitable for SCM development, home appliance control. It uses a 5V~12V TIL control signal which can control DC / AC signal.
